# Fritzing sketch Diagrama (saved by Fritzing 0.9.3b)

parts:
  Part1 = Arduino Uno (Rev3)
  SM1 = 28BYJ-48 Stepper Motor [part_number=28BYJ-48]
  Driver1 = 28BYJ-48 Driver Module [part_number=ULN2003 package=THT]

nets:
  N1: Part1.D8, Driver1.IN1
  N2: Part1.D9_PWM, Driver1.IN2
  N3: Part1.D10_PWM/SS, Driver1.IN3
  N4: Part1.D11_PWM/MOSI, Driver1.IN4
  N5: Part1.5V, Driver1.Vmotor
  GND: Part1.GND, Driver1.GND
  N6: SM1.blue-pin, Driver1.blue-pin
  N7: SM1.pink-pin, Driver1.pink-pin
  N8: SM1.yellow-pin, Driver1.yellow-pin
  N9: SM1.orange-pin, Driver1.orange-pin
  N10: SM1.red-pin, Driver1.red-pin

custom parts:
  28BYJ-48 Stepper Motor: Unipolar Stepper Motor 28BYJ-48 Top coil - pink & orange Bottom coil - blue & yellow Common rail - red Connector pins: blue - pink - yellow - orange - red
  28BYJ-48 Driver Module: ULN2003 Driver Module for the 28BYJ-48 Unipolar Stepper Motor LED A - Blue wire - Bottom coil left LED B - Pink wire - Top coil left LED C - Yellow wire - Bottom coil right LED D - Orange wire - Top coil right Common rail - red Connector pins: blue - pink - yellow - orange - red Control pins - IN1 to IN4 Power pins - GND & Vmotor (5-12V) On/Off jumper (if removed, power to motor is cut).
